// Logisim project Automatic show StopOn_3 in 7-segment display using mux and flipflop.circ as structural Verilog: 1 circuit, main circuit main
module main (
);

  wire and_1_out, and_2_out, clock_1_out, j_k_ff_2_qn, j_k_ff_3_q, j_k_ff_3_qn, multiplexer_1_out,
       multiplexer_2_out, multiplexer_3_out, multiplexer_4_out, multiplexer_5_out, multiplexer_6_out,
       multiplexer_7_out;
  wire [1:0] j_k_ff_2_q;

  Multiplexer #(.select(2)) multiplexer_1 (
    .in0(j_k_ff_3_qn), .in1(j_k_ff_3_q), .in2(j_k_ff_3_qn), .in3(j_k_ff_3_q), .out(multiplexer_1_out),
    .sel(j_k_ff_2_q));  // open: en
  Multiplexer #(.select(2)) multiplexer_2 (
    .in0(1'b0), .in1(j_k_ff_3_q), .in2(j_k_ff_3_qn), .in3(j_k_ff_3_q), .out(multiplexer_2_out),
    .sel(j_k_ff_2_q));  // open: en
  Multiplexer #(.select(2)) multiplexer_3 (
    .in0(j_k_ff_3_qn), .in1(j_k_ff_3_qn), .in2(1'b1), .in3(j_k_ff_3_q), .out(multiplexer_3_out),
    .sel(j_k_ff_2_q));  // open: en
  Multiplexer #(.select(2)) multiplexer_4 (
    .in0(1'b1), .in1(j_k_ff_3_qn), .in2(j_k_ff_3_qn), .in3(1'b1), .out(multiplexer_4_out), .sel(j_k_ff_2_q));  // open: en
  Multiplexer #(.select(2)) multiplexer_5 (
    .in0(j_k_ff_3_q), .in1(1'b1), .in2(1'b1), .in3(1'b0), .out(multiplexer_5_out), .sel(j_k_ff_2_q));  // open: en
  Multiplexer #(.select(2)) multiplexer_6 (
    .in0(1'b1), .in1(j_k_ff_3_q), .in2(j_k_ff_3_qn), .in3(1'b0), .out(multiplexer_6_out), .sel(j_k_ff_2_q));  // open: en
  Multiplexer #(.select(2)) multiplexer_7 (
    .in0(1'b1), .in1(1'b1), .in2(j_k_ff_3_q), .in3(j_k_ff_3_q), .out(multiplexer_7_out), .sel(j_k_ff_2_q));  // open: en
  _7_Segment_Display u_7_segment_display_1 (
    .g(multiplexer_7_out), .f(multiplexer_6_out), .a(multiplexer_1_out), .b(multiplexer_2_out),
    .e(multiplexer_5_out), .d(multiplexer_4_out), .c(multiplexer_3_out), .dp(1'b1));
  Clock clock_1 (.out(clock_1_out));
  J_K_Flip_Flop j_k_ff_1 (
    .J(and_2_out), .clk(clock_1_out), .K(and_2_out), .Q(j_k_ff_2_q[1]));  // open: Qn, preset, en, reset
  and and_1 (and_1_out, j_k_ff_2_qn, j_k_ff_3_q);
  and and_2 (and_2_out, j_k_ff_3_q, j_k_ff_2_q[0]);
  J_K_Flip_Flop j_k_ff_2 (
    .J(and_1_out), .clk(clock_1_out), .K(and_2_out), .Q(j_k_ff_2_q[0]), .Qn(j_k_ff_2_qn));  // open: preset, en, reset
  J_K_Flip_Flop j_k_ff_3 (
    .J(j_k_ff_3_qn), .clk(clock_1_out), .K(j_k_ff_3_q), .Q(j_k_ff_3_q), .Qn(j_k_ff_3_qn));  // open: preset, en, reset
endmodule
